// Logisim project alu.circ as structural Verilog: 2 circuits, main circuit main
module main (
  input  b0,
  input  b1,
  input  b2,
  input  b3,
  input  a0,
  input  a1,
  input  a2,
  input  a3,
  input  c0,
  input  c1,
  output K1,
  output K2,
  output o0,
  output o1,
  output o2,
  output o3
);

  wire main_1_s0, main_1_s1, main_1_s2, main_1_s3, main_2_p0, main_2_p1, main_2_p2, main_2_p3, or_all_1_o0,
       or_all_1_o1, or_all_1_o2, or_all_1_o3;

  addsub_main main_1 (
    .b3(b3), .b2(b2), .b1(b1), .b0(b0), .a3(a3), .a2(a2), .a1(a1), .a0(a0), .sub(c1), .s3(main_1_s3),
    .s2(main_1_s2), .s1(main_1_s1), .s0(main_1_s0));  // open: s4
  greater_equal greater_equal_1 (.b0(b0), .b1(b1), .b2(b2), .b3(b3), .a0(a0), .a1(a1), .a2(a2), .a3(a3), .K1(K2));
  multiplier_main main_2 (
    .b1(b1), .b0(b0), .a1(a1), .a0(a0), .p3(main_2_p3), .p2(main_2_p2), .p1(main_2_p1), .p0(main_2_p0));
  or_all or_all_1 (
    .b3(b3), .b2(b2), .b1(b1), .b0(b0), .a3(a3), .a2(a2), .a1(a1), .a0(a0), .o3(or_all_1_o3),
    .o2(or_all_1_o2), .o1(or_all_1_o1), .o0(or_all_1_o0));
  not not_1 (K1, K2);
  mux2_main main_3 (.D0(main_1_s0), .D1(main_1_s0), .D2(main_2_p0), .D3(or_all_1_o0), .S1(c1), .S0(c0), .Y(o0));
  mux2_main main_4 (.D0(main_1_s1), .D1(main_1_s1), .D2(main_2_p1), .D3(or_all_1_o1), .S1(c1), .S0(c0), .Y(o1));
  mux2_main main_5 (.D0(main_1_s2), .D1(main_1_s2), .D2(main_2_p2), .D3(or_all_1_o2), .S1(c1), .S0(c0), .Y(o2));
  mux2_main main_6 (.D0(main_1_s3), .D1(main_1_s3), .D2(main_2_p3), .D3(or_all_1_o3), .S1(c1), .S0(c0), .Y(o3));
endmodule

// Or
module or_all (
  input  b3,
  input  b2,
  input  b1,
  input  b0,
  input  a3,
  input  a2,
  input  a1,
  input  a0,
  output o3,
  output o2,
  output o1,
  output o0
);

  or or_1 (o0, b0, a0);
  or or_2 (o1, b1, a1);
  or or_3 (o2, b2, a2);
  or or_4 (o3, b3, a3);
endmodule
