// Logisim project addsub.circ as structural Verilog: 2 circuits, main circuit main
module main (
  input  b3,
  input  b2,
  input  b1,
  input  b0,
  input  a3,
  input  a2,
  input  a1,
  input  a0,
  input  sub,
  output s4,
  output s3,
  output s2,
  output s1,
  output s0
);

  wire xor_1_out, xor_2_out, xor_3_out, xor_4_out;

  xor xor_1 (xor_1_out, b3, sub);
  xor xor_2 (xor_2_out, b2, sub);
  xor xor_3 (xor_3_out, b1, sub);
  xor xor_4 (xor_4_out, b0, sub);
  _4Bit_Adder u_4bit_adder_1 (
    .b3(xor_1_out), .b2(xor_2_out), .b1(xor_3_out), .b0(xor_4_out), .a3(a3), .a2(a2), .a1(a1), .a0(a0),
    .s4(s4), .s3(s3), .s2(s2), .s1(s1), .s0(s0), .sub(sub));
endmodule

// 4-Bit Adder
module _4Bit_Adder (
  input  b3,
  input  b2,
  input  b1,
  input  b0,
  input  a3,
  input  a2,
  input  a1,
  input  a0,
  input  sub,
  output s4,
  output s3,
  output s2,
  output s1,
  output s0
);

  wire adder_2_cout, adder_3_cout, adder_4_cout;

  Adder #(.width(1)) adder_1 (.a(a3), .b(b3), .out(s3), .cin(adder_2_cout), .cout(s4));
  Adder #(.width(1)) adder_2 (.a(a2), .b(b2), .out(s2), .cin(adder_3_cout), .cout(adder_2_cout));
  Adder #(.width(1)) adder_3 (.a(a1), .b(b1), .out(s1), .cin(adder_4_cout), .cout(adder_3_cout));
  Adder #(.width(1)) adder_4 (.a(a0), .b(b0), .out(s0), .cin(sub), .cout(adder_4_cout));
endmodule
