// Logisim project comparator.circ as structural Verilog: 3 circuits, main circuit main
module main (
  input  b0,
  input  b1,
  input  b2,
  input  b3,
  input  a0,
  input  a1,
  input  a2,
  input  a3,
  output K1
);

  addsub_main main_1 (
    .b3(b3), .b2(b2), .b1(b1), .b0(b0), .a3(a3), .a2(a2), .a1(a1), .a0(a0), .sub(1'b1), .s4(K1));  // open: s3, s2, s1, s0
endmodule

// <
module smaller (
  input  b0,
  input  b1,
  input  b2,
  input  b3,
  input  a0,
  input  a1,
  input  a2,
  input  a3,
  output K1
);

  wire main_1_s4;

  addsub_main main_1 (
    .b3(b3), .b2(b2), .b1(b1), .b0(b0), .a3(a3), .a2(a2), .a1(a1), .a0(a0), .sub(1'b1), .s4(main_1_s4));  // open: s3, s2, s1, s0
  not not_1 (K1, main_1_s4);
endmodule

// >=
module greater_equal (
  input  b0,
  input  b1,
  input  b2,
  input  b3,
  input  a0,
  input  a1,
  input  a2,
  input  a3,
  output K1
);

  addsub_main main_1 (
    .b3(b3), .b2(b2), .b1(b1), .b0(b0), .a3(a3), .a2(a2), .a1(a1), .a0(a0), .sub(1'b1), .s4(K1));  // open: s3, s2, s1, s0
endmodule
