// Logisim project upcounter.circ as structural Verilog: 2 circuits, main circuit main
module main (
);

  wire clock_1_out, t_ff_1_nq, t_ff_1_q, t_ff_2_nq, t_ff_2_q, t_ff_3_nq, t_ff_4_nq, t_ff_4_q;

  Clock clock_1 (.out(clock_1_out));
  // Probe on t_ff_1_nq
  T_FF t_ff_1 (.T(clock_1_out), .Q(t_ff_1_q), .nQ(t_ff_1_nq));
  // Probe on t_ff_2_nq
  T_FF t_ff_2 (.T(t_ff_1_q), .Q(t_ff_2_q), .nQ(t_ff_2_nq));
  // Probe on t_ff_4_nq
  T_FF t_ff_3 (.T(t_ff_4_q), .nQ(t_ff_3_nq));  // open: Q
  T_FF t_ff_4 (.T(t_ff_2_q), .Q(t_ff_4_q), .nQ(t_ff_4_nq));
  // Probe on t_ff_3_nq
endmodule

module T_FF (
  input  T,
  output Q,
  output nQ
);

  D_Flip_Flop D_FF (.clk(T), .D(nQ), .Q(Q), .Qn(nQ));  // open: preset, en, reset
endmodule
