// Logisim project multiplier.circ as structural Verilog: 3 circuits, main circuit main
module main (
  input  b1,
  input  b0,
  input  a1,
  input  a0,
  output p3,
  output p2,
  output p1,
  output p0
);

  wire and_1_out, and_2_out, and_3_out, half_adder_1_c_out;

  and and_1 (and_1_out, a0, b1);
  and and_2 (and_2_out, b1, a1);
  and and_3 (and_3_out, b0, a1);
  Half_Adder half_adder_1 (.c_out(half_adder_1_c_out), .b(and_1_out), .a(and_3_out), .sum(p1));
  Half_Adder half_adder_2 (.c_out(p3), .b(and_2_out), .a(half_adder_1_c_out), .sum(p2));
  and and_4 (p0, a0, b0);
endmodule

// FA
module Full_Adder (
  input  b,
  input  a,
  input  c_in,
  output c_out,
  output sum
);

  wire and_1_out, and_2_out, xor_1_out;

  or or_1 (c_out, and_1_out, and_2_out);
  and and_1 (and_1_out, b, a);
  xor xor_1 (xor_1_out, b, a);
  and and_2 (and_2_out, xor_1_out, c_in);
  xor xor_2 (sum, xor_1_out, c_in);
endmodule

// HA
module Half_Adder (
  input  b,
  input  a,
  output c_out,
  output sum
);

  and and_1 (c_out, a, b);
  xor xor_1 (sum, b, a);
endmodule
