// Logisim project mux2.circ as structural Verilog: 2 circuits, main circuit main
module main (
  input  D0,
  input  D1,
  input  D2,
  input  D3,
  input  S1,
  input  S0,
  output Y
);

  wire MUX_1_2_out_4, MUX_1_out_4;

  MUX_1 MUX_1 (.in_1(D0), .in_2(D1), .in_3(S1), .out_4(MUX_1_out_4));
  MUX_1 MUX_1_2 (.in_1(D2), .in_2(D3), .in_3(S1), .out_4(MUX_1_2_out_4));
  MUX_1 MUX_1_3 (.in_1(MUX_1_out_4), .in_2(MUX_1_2_out_4), .in_3(S0), .out_4(Y));
endmodule

module MUX_1 (
  input  in_1,
  input  in_2,
  input  in_3,
  output out_4
);

  wire and_1_out, and_2_out, not_1_out;

  and and_1 (and_1_out, in_1, not_1_out);
  not not_1 (not_1_out, in_3);
  and and_2 (and_2_out, in_2, in_3);
  or or_1 (out_4, and_1_out, and_2_out);
endmodule
